// Logisim project ArqCompPract1.circ as structural Verilog: 1 circuit, main circuit main
module main (
);

  Register A ();  // open: D, en, Q, clk, clr
  Adder adder_1 ();  // open: a, b, out, cin, cout
  Register B ();  // open: D, en, Q, clk, clr
  BitSelector #(.width(1), .group(10)) bitselector_1 ();  // open: in, out, sel
  Register IR ();  // open: D, en, Q, clk, clr
  Register MAR ();  // open: D, en, Q, clk, clr
  Register MBR ();  // open: D, en, Q, clk, clr
  Register PC ();  // open: D, en, Q, clk, clr
  RAM #(.dataWidth(32)) ram_1 ();  // open: addr, data, sel, clk, ld, clr
endmodule
