// Logisim project Pract1.circ as structural Verilog: 6 circuits, main circuit main
module main (
  input  [3:0] in_1
);

  wire Clock, decoder_1_out0, decoder_1_out1, decoder_1_out2, decoder_1_out3, decoder_1_out4, decoder_1_out5,
       decoder_1_out6, decoder_1_out7, decoder_2_out0, decoder_2_out1, decoder_2_out2, decoder_2_out3,
       decoder_2_out4, decoder_2_out5, decoder_2_out6, decoder_2_out7, decoder_2_out8, decoder_2_out9,
       n_1_out, not_1_out, not_2_out, or_1_out, or_2_out, or_3_out, or_4_out, or_5_out, or_6_out, Reset, X0,
       X1, X2, X3, X4, X5, X6, X7, X8, X9, X10, X11, X12, X13, X14, X15, X16;
  wire [2:0] counter_1_q;
  wire [3:0] bitselector_1_out, IR_q;
  wire [7:0] A, B, MAR_q, MBR, multiplexer_1_out, multiplexer_2_out, multiplexer_3_out, PC, ram_1_data, Sum;

  Button button_1 (.out(Reset));
  or or_1 (or_1_out, X7, X14);
  Counter #(.width(3), .max('h7)) counter_1 (
    .load(X5), .D(3'b000), .count(not_1_out), .Q(counter_1_q), .clk(Clock), .clr(Reset));  // open: carry
  not not_1 (not_1_out, X5);
  Clock clock_1 (.out(Clock));
  A a_1 (.Data(MBR), .Inc(X14), .Load(or_1_out), .Clock(Clock), .Reset(or_2_out), .out_6(A));
  or or_2 (or_2_out, X11, Reset);
  Register #(.width(4)) IR (.D(bitselector_1_out), .en(X3), .Q(IR_q), .clk(Clock), .clr(Reset));
  BitSelector #(.group(4)) bitselector_1 (.in(MBR), .out(bitselector_1_out), .sel(1'b0));
  Decoder #(.select(3), .enable("false")) decoder_1 (
    .out0(decoder_1_out0), .out1(decoder_1_out1), .out2(decoder_1_out2), .out3(decoder_1_out3),
    .out4(decoder_1_out4), .out5(decoder_1_out5), .out6(decoder_1_out6), .out7(decoder_1_out7),
    .sel(counter_1_q));
  Hex_Digit_Display hex_digit_display_1 (.value(IR_q));  // open: dp
  Decoder #(.select(4), .enable("false")) decoder_2 (
    .out0(decoder_2_out0), .out1(decoder_2_out1), .out2(decoder_2_out2), .out3(decoder_2_out3),
    .out4(decoder_2_out4), .out5(decoder_2_out5), .out6(decoder_2_out6), .out7(decoder_2_out7),
    .out8(decoder_2_out8), .out9(decoder_2_out9), .sel(IR_q));  // open: out10, out11, out12, out13, out14, out15
  Multiplexer #(.width(8), .enable("false")) multiplexer_1 (.in0(A), .in1(Sum), .out(multiplexer_1_out), .sel(X10));
  or or_3 (or_3_out, X4, X8, X9, X10);
  B b_1 (.Data(multiplexer_1_out), .Inc(X9), .Compl(X8), .Load(or_3_out), .Clock(Clock), .out_6(B));
  N n_1 (.Data(B), .Enable(X16), .Out(n_1_out));
  UnidadControl unidadcontrol_1 (
    .X0(X0), .X1(X1), .X2(X2), .X3(X3), .X4(X4), .X5(X5), .X6(X6), .X7(X7), .X8(X8), .X9(X9), .X10(X10),
    .X11(X11), .X12(X12), .X13(X13), .X14(X14), .X15(X15), .Q1(decoder_2_out1), .Q2(decoder_2_out2),
    .Q3(decoder_2_out3), .Q4(decoder_2_out4), .Q5(decoder_2_out5), .Q6(decoder_2_out6), .Q7(decoder_2_out7),
    .Q8(decoder_2_out8), .Q9(decoder_2_out9), .T0(decoder_1_out0), .T1(decoder_1_out1), .T2(decoder_1_out2),
    .T3(decoder_1_out3), .T4(decoder_1_out4), .T5(decoder_1_out5), .T6(decoder_1_out6), .T7(decoder_1_out7),
    .X16(X16), .Q0(decoder_2_out0));
  or or_4 (or_4_out, X15, n_1_out);
  Adder adder_1 (.a(A), .b(B), .out(Sum));  // open: cin, cout
  Counter u_PC (.load(or_4_out), .D(MAR_q), .count(X2), .Q(PC), .clk(Clock), .clr(Reset));  // open: carry
  Multiplexer #(.width(8), .enable("false")) multiplexer_2 (.in0(PC), .in1(MBR), .out(multiplexer_2_out), .sel(X6));
  Register MAR (.D(multiplexer_2_out), .en(or_5_out), .Q(MAR_q), .clk(Clock), .clr(Reset));
  or or_5 (or_5_out, X0, X6);
  RAM ram_1 (.addr(MAR_q), .data(ram_1_data), .clk(Clock), .ld(not_2_out));  // open: sel, clr
  not not_2 (not_2_out, X13);
  Hex_Digit_Display hex_digit_display_2 (.value(A[7:4]));  // open: dp
  Hex_Digit_Display hex_digit_display_3 (.value(B[7:4]));  // open: dp
  assign ram_1_data = X13 ? MBR : 8'bz;  // Controlled_Buffer controlled_buffer_1
  Multiplexer #(.width(8), .enable("false")) multiplexer_3 (
    .in0(ram_1_data), .in1(A), .out(multiplexer_3_out), .sel(X12));
  or or_6 (or_6_out, X12, X1);
  Hex_Digit_Display hex_digit_display_4 (.value(A[3:0]));  // open: dp
  Hex_Digit_Display hex_digit_display_5 (.value(B[3:0]));  // open: dp
  Register u_MBR (.D(multiplexer_3_out), .en(or_6_out), .Q(MBR), .clk(Clock), .clr(Reset));
endmodule

// Unidad de Control
module UnidadControl (
  input  Q0,
  input  Q1,
  input  Q2,
  input  Q3,
  input  Q4,
  input  Q5,
  input  Q6,
  input  Q7,
  input  Q8,
  input  Q9,
  input  T0,
  input  T1,
  input  T2,
  input  T3,
  input  T4,
  input  T5,
  input  T6,
  input  T7,
  output X0,
  output X1,
  output X2,
  output X3,
  output X4,
  output X5,
  output X6,
  output X7,
  output X8,
  output X9,
  output X10,
  output X11,
  output X12,
  output X13,
  output X14,
  output X15,
  output X16
);

  wire Q1T3_out, Q1T4_out, Q1T5_out, Q1T6_out, Q6T3_out, Q6T4_out, Q6T5_out, Q8T3_out, Q8T4_out, Q8T5_out,
       Q9T3_out, Q9T4_out, Q9T5_out;

  and Q1T3 (Q1T3_out, Q1, T3);
  and Q6T3 (Q6T3_out, Q6, T3);
  and Q8T3 (Q8T3_out, Q8, T3);
  and Q1T4 (Q1T4_out, Q1, T4);
  and Q1T6 (Q1T6_out, Q1, T6);
  and Q6T4 (Q6T4_out, Q6, T4);
  and Q8T4 (Q8T4_out, Q8, T4);
  and Q0T3 (X4, Q0, T3);
  and Q1T7 (X7, Q1, T7);
  and Q2T3 (X8, Q2, T3);
  and Q3T3 (X9, Q3, T3);
  and Q4T3 (X10, Q4, T3);
  and Q5T3 (X11, Q5, T3);
  and Q6T7 (X13, Q6, T7);
  and Q7T3 (X14, Q7, T3);
  and Q8T6 (X15, Q8, T6);
  and Q9T6 (X16, Q9, T6);
  and Q1T5 (Q1T5_out, Q1, T5);
  and Q6T5 (Q6T5_out, Q6, T5);
  and Q8T5 (Q8T5_out, Q8, T5);
  and Q6T6 (X12, Q6, T6);
  and Q9T5 (Q9T5_out, Q9, T5);
  and Q9T4 (Q9T4_out, Q9, T4);
  and Q9T3 (Q9T3_out, Q9, T3);
  or or_1 (X1, T1, Q1T4_out, Q1T6_out, Q6T4_out, Q8T4_out, Q9T4_out);
  or or_2 (X2, T1, Q1T4_out, Q9T4_out, Q6T4_out);
  or or_3 (X5, X4, X7, X8, X9, X10, X11, X13, X14, X15, X16);
  or or_4 (X6, Q1T5_out, Q6T5_out, Q9T5_out, Q8T5_out);
  or or_5 (X0, T0, Q1T3_out, Q9T3_out, Q6T3_out, Q8T3_out);

  assign X3 = T2;
endmodule

module A (
  input  [7:0] Data,
  input  Inc,
  input  Reset,
  input  Load,
  input  Clock,
  output [7:0] out_6
);

  wire [7:0] adder_1_out, multiplexer_1_out;

  Adder adder_1 (.a(out_6), .b(8'h1), .out(adder_1_out));  // open: cin, cout
  Multiplexer #(.width(8), .enable("false")) multiplexer_1 (
    .in0(Data), .in1(adder_1_out), .out(multiplexer_1_out), .sel(Inc));
  Register register_1 (.D(multiplexer_1_out), .en(Load), .Q(out_6), .clk(Clock), .clr(Reset));
endmodule

module B (
  input  [7:0] Data,
  input  Load,
  input  Inc,
  input  Compl,
  input  Clock,
  output [7:0] out_6
);

  wire [7:0] adder_1_out, multiplexer_1_out, multiplexer_2_out, not_1_out;

  Adder adder_1 (.a(out_6), .b(8'h1), .out(adder_1_out));  // open: cin, cout
  assign not_1_out = ~out_6;  // NOT_Gate not_1, 8 bits wide
  Multiplexer #(.width(8), .enable("false")) multiplexer_1 (
    .in0(Data), .in1(adder_1_out), .out(multiplexer_1_out), .sel(Inc));
  Multiplexer #(.width(8), .enable("false")) multiplexer_2 (
    .in0(multiplexer_1_out), .in1(not_1_out), .out(multiplexer_2_out), .sel(Compl));
  Register register_1 (.D(multiplexer_2_out), .en(Load), .Q(out_6), .clk(Clock));  // open: clr
endmodule

module PC (
  input  [7:0] Data,
  input  Inc,
  input  Load,
  input  Clock,
  output [7:0] Out
);

  wire [7:0] adder_1_out, multiplexer_1_out;

  Adder adder_1 (.a(multiplexer_1_out), .b(8'h1), .out(adder_1_out));  // open: cin, cout
  Multiplexer #(.width(8), .enable("false")) multiplexer_1 (
    .in0(Data), .in1(adder_1_out), .out(multiplexer_1_out), .sel(Inc));
  Register register_1 (.D(multiplexer_1_out), .en(Load), .Q(Out), .clk(Clock));  // open: clr
endmodule

module N (
  input  [7:0] Data,
  input  Enable,
  output Out
);

  wire comparator_1_eq, comparator_1_lt, or_1_out;

  Comparator comparator_1 (.a(Data), .b({8{1'b0}}), .eq(comparator_1_eq), .lt(comparator_1_lt));  // open: gt
  or or_1 (or_1_out, comparator_1_eq, comparator_1_lt);
  and and_1 (Out, or_1_out, Enable);
endmodule
